// Digital circuit alu.dig as structural Verilog
module alu (
  input  [63:0] A,
  input  [63:0] B,
  input  [2:0] ALUOp,
  output [63:0] R
);

  wire [63:0] add_1_s, barrelshifter_1_out, barrelshifter_2_out, barrelshifter_3_out, barrelshifter_4_out,
       div_1_r, mul_1_mul, sub_1_s;

  Add #(.Bits(64)) add_1 (.a(A), .b(B), .c_i(1'b0), .s(add_1_s));  // open: c_o
  Sub #(.Bits(64)) sub_1 (.a(A), .b(B), .c_i(1'b0), .s(sub_1_s));  // open: c_o
  Mul #(.Bits(32)) mul_1 (.a(A[31:0]), .b(B[31:0]), .mul(mul_1_mul));
  Div #(.Bits(64)) div_1 (.a(A), .b(B), .r(div_1_r));  // open: q
  BarrelShifter #(.Bits(64)) barrelshifter_1 (.in(A), .shift(B[6:0]), .out(barrelshifter_1_out));
  BarrelShifter #(.Bits(64), .direction("right")) barrelshifter_2 (.in(A), .shift(B[6:0]), .out(barrelshifter_2_out));
  BarrelShifter #(.Bits(64), .barrelShifterMode("arithmetic")) barrelshifter_3 (
    .in(A), .shift(B[6:0]), .out(barrelshifter_3_out));
  BarrelShifter #(.Bits(64), .barrelShifterMode("arithmetic"), .direction("right")) barrelshifter_4 (
    .in(A), .shift(B[6:0]), .out(barrelshifter_4_out));
  Multiplexer #(.Selector_Bits(3), .Bits(64)) multiplexer_1 (
    .sel(ALUOp), .in_0(add_1_s), .in_1(sub_1_s), .in_2(mul_1_mul), .in_3(div_1_r),
    .in_4(barrelshifter_1_out), .in_5(barrelshifter_2_out), .in_6(barrelshifter_3_out),
    .in_7(barrelshifter_4_out), .out(R));
endmodule
