// Digital circuit lab07-part1.dig as structural Verilog
module lab07_part1 (
  input  CLK,
  input  EN,
  input  CLR,
  input  PROG,
  output [63:0] A0,
  output [63:0] A1,
  output [63:0] A2,
  output DONE
);

  wire ALUSrcB, and_2_out, CLK_t, rd, RFW, rs1, rs2, x0, x1, x2, x3, x4, x5, x6, x7, x8, x9, x13, x14, x15,
       x16, x17, x18, x19, x20, x21, x22, x23, x24, x25, x26, x27, x28, x29, x30, x31;
  wire [2:0] ALUOp;
  wire [31:0] iw;
  wire [63:0] _64_bit_register_1_p1, imm_I, multiplexer_1_out, PC, register_file_1_p3, register_file_1_p8,
       register_file_1_p9;

  // Probe on PC
  // Probe on iw
  // Probe on rs1
  // Probe on rs2
  // Probe on rd
  // Probe on imm_I
  // _64_bit_register _64_bit_register_1: pin names not known; wires that end beside it: _64_bit_register_1_p1, CLR, EN, CLK_t, PC
  and and_1 (CLK_t, CLK, ~DONE);  // And
  Comparator #(.Bits(32)) END (.a(iw), .b(32'hc0001073), .eq(DONE));  // open: gt, lt
  LED led_1 (.in(DONE));
  // Probe on x0
  // Probe on x1
  // Probe on x2
  // Probe on x3
  // Probe on x4
  // Probe on x5
  // Probe on x6
  // Probe on x7
  // instruction_memory1 instruction_memory1_1: pin names not known; wires that end beside it: PROG, PC[9:2], iw
  Add #(.Bits(64)) PC_plus_4 (.a(PC), .b(64'h4), .c_i(1'b0), .s(_64_bit_register_1_p1));  // open: c_o
  // Probe on x8
  // Probe on x9
  // Probe on A0
  // Probe on A1
  // Probe on A2
  // Probe on x13
  // Probe on x14
  // Probe on x15
  // InstDecoder instdecoder_1: pin names not known; wires that end beside it: iw, ALUSrcB, ALUOp, RFW
  // RegDecoder regdecoder_1: pin names not known; wires that end beside it: iw, rs1, rs2, rd
  // ImmDecoder immdecoder_1: pin names not known; wires that end beside it: iw, imm_I
  // Probe on x16
  // Probe on x17
  // Probe on x18
  // Probe on x19
  // Probe on x20
  // Probe on x21
  // Probe on x22
  // Probe on x23
  and and_2 (and_2_out, RFW, EN);
  // Probe on x24
  // Probe on x25
  // Probe on x26
  // Probe on x27
  // Probe on x28
  // Probe on x29
  // Probe on x30
  // Probe on x31
  // register_file register_file_1: pin names not known; wires that end beside it: rs1, rs2, register_file_1_p3, and_2_out, rd, CLK_t, CLR, register_file_1_p8, register_file_1_p9, x0, x1, x2, x3, x4, x5, x6, x7, x8, x9, A0, A1, A2, x13, x14, x15, x16, x17, x18, x19
  Multiplexer #(.Bits(64)) multiplexer_1 (
    .sel(ALUSrcB), .in_0(register_file_1_p9), .in_1(imm_I), .out(multiplexer_1_out));
  alu alu_1 (.A(register_file_1_p8), .B(multiplexer_1_out), .ALUOp(ALUOp), .R(register_file_1_p3));

  // Other names for the same wires on the sheet: x10[63:0] = A0; x11[63:0] = A1; x12[63:0] = A2
endmodule
